// Digital circuit Parallelschaltung Blackbox Bauplan.dig as structural Verilog
module Parallelschaltung_Blackbox_Bauplan (
);

  wire parallelschaltung_blackbox_1_d1, S1_a, S1_b, S2_a, S2_b;

  Switch S2 (.A(S2_a), .B(S2_b));
  Switch S1 (.A(S1_a), .B(S1_b));
  Parallelschaltung_Blackbox parallelschaltung_blackbox_1 (
    .Vcc(1'b1), .S12(S1_a), .S22(S2_a), .S11(S1_b), .S21(S2_b), .D1(parallelschaltung_blackbox_1_d1));
  LED led_1 (.in(parallelschaltung_blackbox_1_d1));
endmodule
