// Digital circuit Parallelschaltung Wahrheitstabelle.dig as structural Verilog
module Parallelschaltung_Wahrheitstabelle (
);

  wire S11_b;

  Switch S11 (.A(1'b1), .B(S11_b));
  Switch S21 (.A(1'b1), .B(S11_b));
  LED D1 (.in(S11_b));
endmodule
