// Digital circuit Parallelschaltung mit zwei Schaltern.dig as structural Verilog
module Parallelschaltung_mit_zwei_Schaltern (
);

  wire S1_b;

  Switch S1 (.A(1'b1), .B(S1_b));
  Switch S2 (.A(1'b1), .B(S1_b));
  LED D1 (.in(S1_b));
endmodule
