// Digital circuit Reihenschaltung Blackbox Bauplan.dig as structural Verilog
module Reihenschaltung_Blackbox_Bauplan (
);

  wire reihenschaltung_blackbox_1_d1, S1_a, S1_b, S2_a, S2_b;

  Switch S2 (.A(S2_a), .B(S2_b));
  Switch S1 (.A(S1_a), .B(S1_b));
  Reihenschaltung_Blackbox reihenschaltung_blackbox_1 (
    .Vcc(1'b1), .S12(S1_a), .S22(S1_b), .S11(S2_a), .S21(S2_b), .D1(reihenschaltung_blackbox_1_d1));
  LED led_1 (.in(reihenschaltung_blackbox_1_d1));
endmodule
