// Digital circuit Reihenschaltung Wahrheitstabelle.dig as structural Verilog
module Reihenschaltung_Wahrheitstabelle (
);

  wire S11_b, S21_b;

  Switch S11 (.A(1'b1), .B(S11_b));
  Switch S21 (.A(S11_b), .B(S21_b));
  LED D1 (.in(S21_b));
endmodule
