// Digital circuit Reihenschaltung mit zwei Schaltern.dig as structural Verilog
module Reihenschaltung_mit_zwei_Schaltern (
);

  wire S1_b, S2_b;

  Switch S1 (.A(1'b1), .B(S1_b));
  Switch S2 (.A(S1_b), .B(S2_b));
  LED D1 (.in(S2_b));
endmodule
