// Digital circuit Relais.dig as structural Verilog
module Relais (
);

  wire R1_p4, S1_b;

  Switch S1 (.A(1'b1), .B(S1_b));
  // Relay R1: pin names not known; wires that end beside it: S1_b, 1'b0, 1'b1, R1_p4
  LED D1 (.in(R1_p4));
endmodule
