// Digital circuit Test NOT mit Relais.dig as structural Verilog
module Test_NOT_mit_Relais (
  input  a,
  output x
);

  NOT_mit_Relais not_mit_relais_1 (.a(a), .Vcc(1'b1), .GND(1'b0), .x(x));
endmodule
