// Digital circuit Test pTypeRelais.dig as structural Verilog
module Test_pTypeRelais (
  input  G
);

  wire ptyperelais_blackbox_1_d;

  pTypeRelais_Blackbox ptyperelais_blackbox_1 (.G(G), .S(1'b1), .D(ptyperelais_blackbox_1_d));
  LightBulb lightbulb_1 (.A(ptyperelais_blackbox_1_d), .B(1'b0));
endmodule
