// Digital circuit pTypeRelais Blackbox.dig as structural Verilog
module pTypeRelais_Blackbox (
  input  G,
  input  S,
  output D
);

  // RelayDT relaydt_1: pin names not known; wires that end beside it: G, 1'b0, D, S
endmodule
