// Digital circuit N-Kanal MOSFET.dig as structural Verilog
module N_Kanal_MOSFET (
  input  G
);

  wire nfet_1_d;

  NFET nfet_1 (.G(G), .D(nfet_1_d), .S(1'b0));
  LightBulb lightbulb_1 (.A(nfet_1_d), .B(1'b1));
endmodule
