// Digital circuit NAND mit MOSFET.dig as structural Verilog
module NAND_mit_MOSFET (
  input  a,
  input  b,
  input  Vcc,
  input  GND,
  output x
);

  wire nfet_1_s;

  PFET pfet_1 (.G(a), .S(Vcc), .D(x));
  PFET pfet_2 (.G(b), .S(Vcc), .D(x));
  NFET nfet_1 (.G(a), .D(x), .S(nfet_1_s));
  NFET nfet_2 (.G(b), .D(nfet_1_s), .S(GND));
endmodule
