// Digital circuit NAND mit Relais.dig as structural Verilog
module NAND_mit_Relais (
  input  a,
  input  b,
  input  Vcc,
  input  GND,
  output x
);

  wire ntyperelais_blackbox_ii_1_d;

  nTypeRelais_Blackbox_II ntyperelais_blackbox_ii_1 (.G(b), .S(GND), .D(ntyperelais_blackbox_ii_1_d));
  pTypeRelais_Blackbox ptyperelais_blackbox_1 (.G(a), .S(Vcc), .D(x));
  nTypeRelais_Blackbox_II ntyperelais_blackbox_ii_2 (.G(a), .S(ntyperelais_blackbox_ii_1_d), .D(x));
  pTypeRelais_Blackbox ptyperelais_blackbox_2 (.G(b), .S(Vcc), .D(x));
endmodule
