// Digital circuit NOR mit MOSFET.dig as structural Verilog
module NOR_mit_MOSFET (
  input  a,
  input  b,
  input  Vcc,
  input  GND,
  output x
);

  wire pfet_1_d;

  NFET nfet_1 (.G(b), .D(x), .S(GND));
  PFET pfet_1 (.G(a), .S(Vcc), .D(pfet_1_d));
  PFET pfet_2 (.G(b), .S(pfet_1_d), .D(x));
  NFET nfet_2 (.G(a), .D(x), .S(GND));
endmodule
