// Digital circuit NOR mit Relais.dig as structural Verilog
module NOR_mit_Relais (
  input  a,
  input  b,
  input  Vcc,
  input  GND,
  output x
);

  wire ptyperelais_blackbox_1_d;

  nTypeRelais_Blackbox_II ntyperelais_blackbox_ii_1 (.G(b), .S(GND), .D(x));
  pTypeRelais_Blackbox ptyperelais_blackbox_1 (.G(a), .S(Vcc), .D(ptyperelais_blackbox_1_d));
  pTypeRelais_Blackbox ptyperelais_blackbox_2 (.G(b), .S(ptyperelais_blackbox_1_d), .D(x));
  nTypeRelais_Blackbox_II ntyperelais_blackbox_ii_2 (.G(a), .S(GND), .D(x));
endmodule
