// Digital circuit NOT mit MOSFET.dig as structural Verilog
module NOT_mit_MOSFET (
  input  a,
  input  Vcc,
  input  GND,
  output x
);

  PFET pfet_1 (.G(a), .S(Vcc), .D(x));
  NFET nfet_1 (.G(a), .D(x), .S(GND));
endmodule
