// Digital circuit NOT mit Relais.dig as structural Verilog
module NOT_mit_Relais (
  input  a,
  input  Vcc,
  input  GND,
  output x
);

  pTypeRelais_Blackbox ptyperelais_blackbox_1 (.G(a), .S(Vcc), .D(x));
  nTypeRelais_Blackbox_II ntyperelais_blackbox_ii_1 (.G(a), .S(GND), .D(x));
endmodule
