// Digital circuit P-Kanal MOSFET.dig as structural Verilog
module P_Kanal_MOSFET (
  input  G
);

  wire pfet_1_d;

  PFET pfet_1 (.G(G), .S(1'b1), .D(pfet_1_d));
  LightBulb x (.A(pfet_1_d), .B(1'b0));
endmodule
