// Digital circuit Test NAND mit MOSFET.dig as structural Verilog
module Test_NAND_mit_MOSFET (
  input  a,
  input  b,
  output out_3
);

  NAND_mit_MOSFET nand_mit_mosfet_1 (.a(a), .b(b), .Vcc(1'b1), .GND(1'b0), .x(out_3));
endmodule
