// Digital circuit Test NAND mit Relais.dig as structural Verilog
module Test_NAND_mit_Relais (
  input  a,
  input  b,
  output x
);

  NAND_mit_Relais nand_mit_relais_1 (.a(a), .b(b), .Vcc(1'b1), .GND(1'b0), .x(x));
endmodule
