// Digital circuit Test NOR mit MOSFET.dig as structural Verilog
module Test_NOR_mit_MOSFET (
  input  a,
  input  b,
  output out_3
);

  NOR_mit_MOSFET nor_mit_mosfet_1 (.a(a), .b(b), .Vcc(1'b1), .GND(1'b0), .x(out_3));
endmodule
