// Digital circuit Test NOR mit Relais.dig as structural Verilog
module Test_NOR_mit_Relais (
  input  a,
  input  b,
  output x
);

  NOR_mit_Relais nor_mit_relais_1 (.a(a), .b(b), .Vcc(1'b1), .GND(1'b0), .x(x));
endmodule
