// Digital circuit Test NOT mit MOSFET.dig as structural Verilog
module Test_NOT_mit_MOSFET (
  input  a,
  output x
);

  NOT_mit_MOSFET not_mit_mosfet_1 (.a(a), .Vcc(1'b1), .GND(1'b0), .x(x));
endmodule
