// Digital circuit Test nTypeRelais.dig as structural Verilog
module Test_nTypeRelais (
  input  G
);

  wire ntyperelais_blackbox_ii_1_d;

  nTypeRelais_Blackbox_II ntyperelais_blackbox_ii_1 (.G(G), .S(1'b0), .D(ntyperelais_blackbox_ii_1_d));
  LightBulb lightbulb_1 (.A(1'b1), .B(ntyperelais_blackbox_ii_1_d));
endmodule
