// Digital circuit UND Verknüpfung Blackbox.dig as structural Verilog
module \UND_Verknüpfung_Blackbox  (
);

  wire reihenschaltung_blackbox_1_d1, S1_a, S1_b, S2_a, S2_b;

  Switch S1 (.A(S1_a), .B(S1_b));
  Switch S2 (.A(S2_a), .B(S2_b));
  Reihenschaltung_Blackbox reihenschaltung_blackbox_1 (
    .Vcc(S1_a), .S12(S1_b), .S22(S2_a), .S11(S2_b), .S21(1'b1), .D1(reihenschaltung_blackbox_1_d1));
  LED D1 (.in(reihenschaltung_blackbox_1_d1));
endmodule
