// Digital circuit nTypeRelais Blackbox I.dig as structural Verilog
module nTypeRelais_Blackbox_I (
  input  G,
  input  S,
  output D
);

  // Relay relay_1: pin names not known; wires that end beside it: G, S, D, S
endmodule
