// Digital circuit nTypeRelais Blackbox II.dig as structural Verilog
module nTypeRelais_Blackbox_II (
  input  G,
  input  S,
  output D
);

  // Relay relay_1: pin names not known; wires that end beside it: G, 1'b0, D, S
endmodule
